# Fritzing sketch Untitled Sketch 2 (saved by Fritzing 0.9.4)
breadboards: 1

parts:
  WeMos_D1_Mini_OLED_Shield1 = WeMos D1 Mini OLED Shield  # not connected
  元件1 = Arduino GPS Shield
  LED1 = RGB LED (6 legs) [package="5 mm [THT]"]  # not connected
  R1 = Temperature Sensor (Thermistor) [thermistor_type=NTC package=THT]  # not connected
  元件2 = Bluetooth Module Breakout - Roving Networks (RN-41)  # not connected
  pH_Circuit1 = pH Circuit  # not connected
  元件3 = RFID USB Reader  # not connected
  VCC1 = Battery block 9V  # not connected
  U2 = EDISON  # not connected
  S1 = Toggle Switch [package=THT]  # not connected
  pH_Circuit2 = pH Circuit  # not connected
  pH_Circuit3 = pH Circuit  # not connected
  元件4 = Bluetooth Module Breakout - Roving Networks (RN-41)  # not connected
  LDH-45-350B1 = LDH-45-350B [package=THT]
  M1 = STM32F103C8T6 blue mini board

nets:
  GND: 元件1.GND, LDH-45-350B1.Vout-, M1.G, M1.GND
  N1: 元件1.RX, M1.A9
  N2: 元件1.TX, M1.A10
  3.3V: 元件1.3.3V, M1.3.3V
  N3: LDH-45-350B1.Vout+, M1.5V
